# Fritzing sketch Centrífuga-Fritzing (saved by Fritzing 0.9.3b)
breadboards: 1

parts:
  S1_Power_Switch = Pushbutton [package=THT]
  Power_plug1_-_12V = Power plug
  U1_-_ESC_control = mystery part, 3 pins [chip_label="ESC C" spacing=300mil]
  U2_-_ESC_power = mystery part, 2 pins [chip_label=ESC spacing=300mil]
  U3_-_Infrared = mystery part, 4 pins [chip_label=Infrared spacing=300mil]
  R1_-_220 = Resistor [tolerance=±5% resistance=220 package=THT]
  R2_-_6_8K = Resistor [tolerance=±5% resistance=6.8k package=THT]
  R1_-_Rotary_encoder = Rotary Potentiometer (Small) [maximum_resistance=100kΩ package=THT]
  LCD1 = LCD screen
  Arduino1 = Arduino Uno (Rev3)
  S1 = Pushbutton [package="[THT]"]
  R1 = Resistor [tolerance=±5% resistance=1k package=THT]

nets:
  N1: S1_Power_Switch.leg0, Power_plug1_-_12V.VCC
  N2: S1_Power_Switch.leg1, U2_-_ESC_power.pin2
  N3: Power_plug1_-_12V.GND, U2_-_ESC_power.pin1
  N4: U1_-_ESC_control.pin1, U3_-_Infrared.pin2, R1_-_Rotary_encoder.wiper, LCD1.LED-, Arduino1.GND, R1.Pin_1
  VDD: U1_-_ESC_control.pin2, R1_-_220.Pin_0, R2_-_6_8K.Pin_1, LCD1.VDD, Arduino1.5V, S1.Pin_3, S1.Pin_4
  N5: U1_-_ESC_control.pin3, Arduino1.D13/SCK
  N6: U3_-_Infrared.pin1, R2_-_6_8K.Pin_0, Arduino1.D6_PWM
  N7: U3_-_Infrared.pin3, R1_-_220.Pin_1
  N8: R1_-_Rotary_encoder.leg1, Arduino1.D8
  N9: R1_-_Rotary_encoder.leg2, Arduino1.D9_PWM
  N10: LCD1.VSS, LCD1.V0, LCD1.R/W
  N11: LCD1.RS, Arduino1.D12/MISO
  N12: LCD1.E, Arduino1.D11_PWM/MOSI
  N13: LCD1.DB4, Arduino1.D5_PWM
  N14: LCD1.DB5, Arduino1.D4
  N15: LCD1.DB6, Arduino1.D3_PWM
  N16: LCD1.DB7, Arduino1.D2
  N17: LCD1.LED+, Arduino1.D7
  N18: Arduino1.D10_PWM/SS, S1.Pin_1, S1.Pin_2, R1.Pin_0

notes:
  ESC signal
  Rotary Encoder
  Infrared RPM sensor
  Power switch
  12V power supply
  ESC power
  Push Button
  12 V Power Supply
  Power Switch
  ESC Power Connector
  Push button
  The ESC is a 5V source
  1 is GND, 2 = Vcc, 3 = signal
  Infrared sensor
  Rotary encoder
