# Fritzing sketch Incubadora-Fritzing (saved by Fritzing 0.9.3b)
breadboards: 1

parts:
  80mm_Fan = DC Motor
  MOSFET1 = Basic FET N-Channel [package="TO220 [THT]"]
  Pushbutton_1 = Pushbutton [package="[THT]"]
  Pushbutton_2 = Pushbutton [package="[THT]"]
  R6_-_Pull_down_for_MOSFET_1 = Resistor [tolerance=±5% resistance=10k package=THT]
  Diode1 = Rectifier Diode [part_number=1N4001 package="300 mil [THT]"]
  Power_plug1 = Power plug
  R8_-_Pull_up_for_Temp1 = Resistor [tolerance=±5% resistance=10k package=THT]
  R9_-_Pull_down_for_button_1 = Resistor [tolerance=±5% resistance=10k package=THT]
  Arduino1 = Arduino Uno (Rev3)
  LCD2 = LCD screen
  MOSFET2 = Basic FET N-Channel [package="TO220 [THT]"]
  R6_-_Pull_down_for_MOSFET_2 = Resistor [tolerance=±5% resistance=10k package=THT]
  R2 = Resistor [tolerance=±5% resistance=1.5 power=22W package=THT]
  R10_-_Pull_down_for_button_2 = Resistor [tolerance=±5% resistance=10k package=THT]
  R1 = Temperature Sensor (Thermistor) [thermistor_type=NTC package=THT]

nets:
  VCC: 80mm_Fan.pin_1, Diode1.cathode, Power_plug1.VCC, Arduino1.VIN, R2.Pin_0
  N1: 80mm_Fan.pin_2, MOSFET1.drain, Diode1.anode
  N2: MOSFET1.gate, R6_-_Pull_down_for_MOSFET_1.Pin_1, Arduino1.D6_PWM
  GND: MOSFET1.source, R6_-_Pull_down_for_MOSFET_1.Pin_0, Power_plug1.GND, R9_-_Pull_down_for_button_1.Pin_1, Arduino1.GND, LCD2.VSS, LCD2.V0, LCD2.R/W, LCD2.LED-, MOSFET2.source, R6_-_Pull_down_for_MOSFET_2.Pin_0, R10_-_Pull_down_for_button_2.Pin_1, R1.pin_0
  N3: Pushbutton_1.Pin_1, Pushbutton_1.Pin_2, R9_-_Pull_down_for_button_1.Pin_0, Arduino1.D9_PWM
  5V: Pushbutton_1.Pin_3, Pushbutton_1.Pin_4, Pushbutton_2.Pin_3, Pushbutton_2.Pin_4, R8_-_Pull_up_for_Temp1.Pin_0, Arduino1.5V, LCD2.VDD
  N4: Pushbutton_2.Pin_1, Pushbutton_2.Pin_2, Arduino1.D10_PWM/SS, R10_-_Pull_down_for_button_2.Pin_0
  N5: R8_-_Pull_up_for_Temp1.Pin_1, Arduino1.A0, R1.pin_1
  N6: Arduino1.D8, MOSFET2.gate, R6_-_Pull_down_for_MOSFET_2.Pin_1
  N7: Arduino1.D11_PWM/MOSI, LCD2.E
  N8: Arduino1.D12/MISO, LCD2.RS
  N9: Arduino1.D2, LCD2.DB7
  N10: Arduino1.D3_PWM, LCD2.DB6
  N11: Arduino1.D4, LCD2.DB5
  N12: Arduino1.D5_PWM, LCD2.DB4
  N13: Arduino1.D7, LCD2.LED+
  N14: MOSFET2.drain, R2.Pin_1

notes:
  Fan
  Temp Sensor
  Botões de Interface
  Botões
  Fan controller
  12V power supply
  Placa de Aquecimento
  12V input
