# Fritzing sketch Thermocycler-Fritzing (saved by Fritzing 0.9.3b)
breadboards: 1

parts:
  Q1 = Basic FET N-Channel [package="TO220 [THT]"]
  Q3 = Basic FET N-Channel [package="TO220 [THT]"]
  R3 = Rotary Potentiometer (Small) [maximum_resistance=100kΩ package=THT]
  S3 = Pushbutton [package="[THT]"]
  Q2 = Basic FET N-Channel [package="TO220 [THT]"]
  R8 = Resistor [tolerance=±5% resistance=10k package=THT]
  R9 = Resistor [tolerance=±5% resistance=10k package=THT]
  D1 = Rectifier Diode [part_number=1N4001 package="Melf DO-213 AB [SMD]"]
  M4 = DC Motor
  J4 = Power Jack [package=power_jack_smd]
  U3 = SWITCH-SPST-2 [package=r_sw_th]
  LCD2 = LCD screen  # not connected
  R15 = Resistor [tolerance=±5% resistance=10k package=THT]
  R16 = Resistor [tolerance=±5% resistance=6.8 package="2512 [SMD]"]
  R17 = Resistor [tolerance=±5% resistance=6.8 package="2512 [SMD]"]
  R18 = Resistor [tolerance=±5% resistance=10k package=THT]
  R19 = Resistor [tolerance=±5% resistance=10k package=THT]
  Part2 = Arduino Leonardo (Rev3b)
  R20 = Temperature Sensor (Thermistor) [thermistor_type=NTC package=THT]
  R21 = Temperature Sensor (Thermistor) [thermistor_type=NTC package=THT]
  R7 = Resistor [tolerance=±2% resistance=100k package=THT]

nets:
  N1: Q1.gate, Part2.D7, R7.Pin_1
  N2: Q1.drain, R17.Pin_1
  N3: Q1.source, Q3.source, R3.wiper, Q2.source, R8.Pin_0, R9.Pin_0, J4.GNDBREAK, R15.Pin_0, R18.Pin_0, R19.Pin_1, Part2.GND, R7.Pin_0
  N4: Q3.gate, R8.Pin_1, Part2.D6_PWM/A7
  N5: Q3.drain, R16.Pin_1
  N6: R3.leg1, Part2.D1/TX
  N7: R3.leg2, Part2.D0/RX
  N8: S3.Pin_1, Part2.5V, R20.pin_0, R21.pin_0
  N9: S3.Pin_3, S3.Pin_4, R19.Pin_0, Part2.D11_PWM
  N10: Q2.gate, R9.Pin_1, Part2.D5_PWM
  N11: Q2.drain, D1.anode, M4.pin_2
  N12: D1.cathode, M4.pin_1, U3.O, R16.Pin_0, R17.Pin_0, Part2.VIN
  N13: J4.PWR, U3.P
  N14: R15.Pin_1, Part2.A0, R21.pin_1
  N15: R18.Pin_1, Part2.A1, R20.pin_1

notes:
  Resistores de cerâmica
  Fan
  12V power Supply
  Rotary encoder
  10K Resistor +
  Push Button
  Mosfets
  10K Thermistors
  Interruptor do sistema
