# Fritzing sketch Webcam-Espectrofotômetro-Fritzing (saved by Fritzing 0.9.3b)
breadboards: 1

parts:
  LED1 = LED - 5mm [color="White (4500K)" package="5 mm [THT]"]
  R1 = Resistor [tolerance=±5% resistance=220 package=THT]
  Power_plug1 = Power plug
  S1 = Pushbutton [package=THT]

nets:
  N1: LED1.cathode, S1.leg1
  N2: LED1.anode, R1.Pin_1
  N3: R1.Pin_0, Power_plug1.VCC
  N4: Power_plug1.GND, S1.leg0
